# Fritzing sketch LDR Synth (saved by Fritzing 0.9.3b)
circuit board: 31.3261cm x 9.80813cm

parts:
  U1 = LM 358 Dual Op-Amp [part_number=LM358 package="DIP8 [THT]"]
  U2 = LM 358 Dual Op-Amp [package="DIP8 [THT]"]
  U3 = LM 358 Dual Op-Amp [package="DIP8 [THT]"]
  U5 = LM 358 Dual Op-Amp [package="DIP8 [THT]"]
  S1 = Pushbutton [package="[THT]"]
  S2 = Pushbutton [package="[THT]"]
  S3 = Pushbutton [package="[THT]"]
  S4 = Pushbutton [package="[THT]"]
  S5 = Pushbutton [package="[THT]"]
  S6 = Pushbutton [package="[THT]"]
  S7 = Pushbutton [package="[THT]"]
  S8 = Pushbutton [package="[THT]"]
  R9 = Resistor [tolerance=±5% resistance=10k package=THT]
  R10 = Resistor [tolerance=±5% resistance=100k package=THT]
  R11 = Resistor [tolerance=±5% resistance=100k package=THT]
  R12 = Resistor [tolerance=±5% resistance=100k package=THT]
  R13 = Resistor [tolerance=±5% resistance=100k package=THT]
  R14 = Resistor [tolerance=±5% resistance=47k package=THT]
  R15 = Resistor [tolerance=±5% resistance=22k package=THT]
  R16 = Resistor [tolerance=±5% resistance=47k package=THT]
  C1 = Ceramic Capacitor [capacitance=0.22µF package="100 mil [THT, multilayer]"]
  R18 = Resistor [tolerance=±5% resistance=100k package=THT]
  R19 = Resistor [tolerance=±5% resistance=22k package=THT]
  R20 = Resistor [tolerance=±5% resistance=470k package=THT]
  C2 = Electrolytic Capacitor [capacitance=2.2µF package="100 mil [THT, electrolytic]"]
  R21 = Resistor [tolerance=±5% resistance=22k package=THT]
  R22 = Resistor [tolerance=±5% resistance=47k package=THT]
  R23 = Resistor [tolerance=±5% resistance=4.7k package=THT]
  C3 = Electrolytic Capacitor [capacitance=4.7µF package="100 mil [THT, electrolytic]"]
  R24 = Resistor [tolerance=±5% resistance=47k package=THT]
  R25 = Resistor [tolerance=±5% resistance=22k package=THT]
  Audio_Out = Loudspeaker
  C4 = Electrolytic Capacitor [capacitance=4.7µF package="100 mil [THT, electrolytic]"]
  R26 = Resistor [tolerance=±5% resistance=10k package=THT]
  R27 = Resistor [tolerance=±5% resistance=22k package=THT]
  C5 = Ceramic Capacitor [capacitance=10pF package="100 mil [THT, multilayer]"]
  R28 = Resistor [tolerance=±5% resistance=100k package=THT]
  R29 = Resistor [tolerance=±5% resistance=100k package=THT]
  LDR1 = Photocell (LDR) [package=THT]
  R31 = Resistor [tolerance=±5% resistance=10k package=THT]
  LDR2 = Photocell (LDR) [package=THT]
  C6 = Ceramic Capacitor [capacitance=10pF package="100 mil [THT, multilayer]"]
  R33 = Resistor [tolerance=±5% resistance=330k package=THT]
  U4 = LM 358 Dual Op-Amp [package="DIP8 [THT]"]
  9V = Power plug
  R1 = Trimmer Potentiometer [maximum_resistance=100kΩ package=THT]
  R7 = Trimmer Potentiometer [maximum_resistance=100kΩ package=THT]
  R8 = Trimmer Potentiometer [maximum_resistance=100kΩ package=THT]
  R6 = Trimmer Potentiometer [maximum_resistance=100kΩ package=THT]
  R5 = Trimmer Potentiometer [maximum_resistance=100kΩ package=THT]
  R4 = Trimmer Potentiometer [maximum_resistance=100kΩ package=THT]
  R3 = Trimmer Potentiometer [maximum_resistance=100kΩ package=THT]
  R2 = Trimmer Potentiometer [maximum_resistance=100kΩ package=THT]
  R17 = Rotary Potentiometer (Large) [maximum_resistance=100kΩ package=THT]
  Adjust_to_60k = Trimmer Potentiometer [maximum_resistance=100k package=THT]
  U6 = LM 358 Dual Op-Amp [part_number=LM358 package="DIP8 [THT]"]
  U7 = LM 358 Dual Op-Amp [package="DIP8 [THT]"]
  U8 = LM 358 Dual Op-Amp [package="DIP8 [THT]"]
  U9 = LM 358 Dual Op-Amp [package="DIP8 [THT]"]
  U10 = LM 358 Dual Op-Amp [package="DIP8 [THT]"]
  R34 = Trimmer Potentiometer [maximum_resistance=100kΩ package=THT]
  R35 = Trimmer Potentiometer [maximum_resistance=100kΩ package=THT]
  R36 = Trimmer Potentiometer [maximum_resistance=100kΩ package=THT]
  R37 = Trimmer Potentiometer [maximum_resistance=100kΩ package=THT]
  R38 = Trimmer Potentiometer [maximum_resistance=100kΩ package=THT]
  R39 = Trimmer Potentiometer [maximum_resistance=100kΩ package=THT]
  R40 = Trimmer Potentiometer [maximum_resistance=100kΩ package=THT]
  R41 = Trimmer Potentiometer [maximum_resistance=100kΩ package=THT]
  S9 = Pushbutton [package="[THT]"]
  S10 = Pushbutton [package="[THT]"]
  S11 = Pushbutton [package="[THT]"]
  S12 = Pushbutton [package="[THT]"]
  S13 = Pushbutton [package="[THT]"]
  S14 = Pushbutton [package="[THT]"]
  S15 = Pushbutton [package="[THT]"]
  S16 = Pushbutton [package="[THT]"]
  R42 = Resistor [tolerance=±5% resistance=10k package=THT]
  R43 = Resistor [tolerance=±5% resistance=10k package=THT]
  R44 = Resistor [tolerance=±5% resistance=100k package=THT]
  R45 = Resistor [tolerance=±5% resistance=100k package=THT]
  R46 = Resistor [tolerance=±5% resistance=100k package=THT]
  R47 = Resistor [tolerance=±5% resistance=100k package=THT]
  R48 = Resistor [tolerance=±5% resistance=100k package=THT]
  R49 = Resistor [tolerance=±5% resistance=100k package=THT]
  R50 = Resistor [tolerance=±5% resistance=47k package=THT]
  R51 = Resistor [tolerance=±5% resistance=47k package=THT]
  R52 = Resistor [tolerance=±5% resistance=47k package=THT]
  R53 = Resistor [tolerance=±5% resistance=22k package=THT]
  R54 = Resistor [tolerance=±5% resistance=22k package=THT]
  R55 = Resistor [tolerance=±5% resistance=22k package=THT]
  R56 = Resistor [tolerance=±5% resistance=22k package=THT]
  R57 = Resistor [tolerance=±5% resistance=22k package=THT]
  C7 = Ceramic Capacitor [capacitance=0.22µF package="100 mil [THT, multilayer]"]
  R58 = Rotary Potentiometer (Large) [maximum_resistance=100kΩ package=THT]
  R59 = Resistor [tolerance=±5% resistance=100k package=THT]
  R60 = Resistor [tolerance=±5% resistance=470k package=THT]
  C8 = Electrolytic Capacitor [capacitance=2.2µF package="100 mil [THT, electrolytic]"]
  R61 = Resistor [tolerance=±5% resistance=47k package=THT]
  R62 = Resistor [tolerance=±5% resistance=4.7k package=THT]
  C9 = Electrolytic Capacitor [capacitance=4.7µF package="100 mil [THT, electrolytic]"]
  C10 = Electrolytic Capacitor [capacitance=4.7µF package="100 mil [THT, electrolytic]"]
  Audio_Out1 = Loudspeaker
  C11 = Ceramic Capacitor [capacitance=10pF package="100 mil [THT, multilayer]"]
  C12 = Ceramic Capacitor [capacitance=10pF package="100 mil [THT, multilayer]"]
  LDR3 = Photocell (LDR) [package=THT]
  R63 = Resistor [tolerance=±5% resistance=10k package=THT]
  LDR4 = Photocell (LDR) [package=THT]
  R64 = Resistor [tolerance=±5% resistance=330k package=THT]
  Adjust_to_60k1 = Trimmer Potentiometer [maximum_resistance=100k package=THT]

nets:
  N1: U1.connector0, S1.Pin_1, S1.Pin_2, S2.Pin_1, S2.Pin_2, S3.Pin_1, S3.Pin_2, S4.Pin_1, S4.Pin_2, S5.Pin_1, S5.Pin_2, S6.Pin_1, S6.Pin_2, S7.Pin_1, S7.Pin_2, S8.Pin_2, R14.Pin_1
  N2: U1.connector1, U1.connector4, R10.Pin_0, R11.Pin_1
  N3: U1.connector2, R14.Pin_0, R15.Pin_0
  GND: U1.connector3, U2.connector3, U3.connector3, U5.connector3, R11.Pin_0, R12.Pin_0, R23.Pin_0, Audio_Out.pin2, R27.Pin_0, R28.Pin_0, U4.connector3, 9V.GND, R17.leg1, U6.connector3, U7.connector3, U8.connector3, U9.connector3, U10.connector3, R45.Pin_0, R47.Pin_0, R48.Pin_0, R53.Pin_0, R58.leg1, R62.Pin_0, Audio_Out1.pin2
  N4: U1.connector5, R9.Pin_0, C1.1
  N5: U1.connector6, U3.connector1, R15.Pin_1, C1.0
  9V: U1.connector7, U2.connector7, U3.connector7, U5.connector7, R10.Pin_1, R13.Pin_1, R29.Pin_1, U4.connector7, 9V.VCC, R17.leg2, U6.connector7, U7.connector7, U8.connector7, U9.connector7, U10.connector7, R44.Pin_1, R46.Pin_1, R49.Pin_1, R58.leg2
  N6: U2.connector0, R16.Pin_1, R20.Pin_1
  N7: U2.connector1, U2.connector4, R12.Pin_1, R13.Pin_0
  N8: U2.connector2, R16.Pin_0, R19.Pin_0
  N9: U2.connector5, R20.Pin_0, C2.-
  N10: U2.connector6, R18.Pin_0, R19.Pin_1, C2.+
  N11: U3.connector0, R22.Pin_1
  N12: U3.connector2, U3.connector6, R21.Pin_1
  N13: U3.connector4, R17.wiper
  N14: U3.connector5, R18.Pin_1, R21.Pin_0
  N15: U5.connector0, R26.Pin_1, C5.0
  N16: U5.connector1, C5.1, LDR2.pin_1
  N17: U5.connector2, R28.Pin_1, R29.Pin_0, U4.connector2
  N18: S1.Pin_3, S1.Pin_4, R1.wiper
  N19: S2.Pin_3, S2.Pin_4, R2.wiper
  N20: S3.Pin_3, S3.Pin_4, R3.wiper
  N21: S4.Pin_3, S4.Pin_4, R4.wiper
  N22: S5.Pin_3, S5.Pin_4, R5.wiper
  N23: S6.Pin_3, S6.Pin_4, R6.wiper
  N24: S7.Pin_3, S7.Pin_4, R7.wiper
  N25: S8.Pin_3, S8.Pin_4, R8.wiper
  N26: R9.Pin_1, R1.leg2, R7.leg2, R8.leg2, R6.leg2, R5.leg2, R4.leg2, R3.leg2, R2.leg2
  N27: R22.Pin_0, R23.Pin_1, C3.+
  N28: C3.-, R24.Pin_0
  N29: R24.Pin_1, R33.Pin_0, U4.connector4
  N30: R25.Pin_0, U4.connector5
  N31: R25.Pin_1, LDR1.pin_0, U4.connector6
  N32: Audio_Out.pin1, C4.-
  N33: C4.+, R26.Pin_0, R27.Pin_1
  N34: LDR1.pin_1, R31.Pin_0
  N35: R31.Pin_1, C6.1, U4.connector1
  N36: LDR2.pin_0, C6.0, U4.connector0, Adjust_to_60k.wiper
  N37: R33.Pin_1, Adjust_to_60k.leg2
  N38: U6.connector0, S9.Pin_2, S10.Pin_1, S10.Pin_2, S11.Pin_1, S11.Pin_2, S12.Pin_1, S12.Pin_2, S13.Pin_1, S13.Pin_2, S14.Pin_1, S14.Pin_2, S15.Pin_1, S15.Pin_2, S16.Pin_1, S16.Pin_2, R52.Pin_1
  N39: U6.connector1, U6.connector4, R48.Pin_1, R49.Pin_0
  N40: U6.connector2, R52.Pin_0, R57.Pin_0
  N41: U6.connector5, R43.Pin_0, C7.1
  N42: U6.connector6, U8.connector1, R57.Pin_1, C7.0
  N43: U7.connector0, R51.Pin_1, R60.Pin_1
  N44: U7.connector1, U7.connector4, R46.Pin_0, R47.Pin_1
  N45: U7.connector2, R51.Pin_0, R56.Pin_0
  N46: U7.connector5, R60.Pin_0, C8.-
  N47: U7.connector6, R56.Pin_1, R59.Pin_0, C8.+
  N48: U8.connector0, R61.Pin_1
  N49: U8.connector2, U8.connector6, R55.Pin_1
  N50: U8.connector4, R58.wiper
  N51: U8.connector5, R55.Pin_0, R59.Pin_1
  N52: U9.connector0, C11.0, LDR4.pin_0, Adjust_to_60k1.wiper
  N53: U9.connector1, C11.1, R63.Pin_1
  N54: U9.connector2, U10.connector2, R44.Pin_0, R45.Pin_1
  N55: U9.connector4, R50.Pin_1, R64.Pin_0
  N56: U9.connector5, R54.Pin_0
  N57: U9.connector6, R54.Pin_1, LDR3.pin_0
  N58: U10.connector0, R42.Pin_1, C12.0
  N59: U10.connector1, C12.1, LDR4.pin_1
  N60: R34.wiper, S16.Pin_3, S16.Pin_4
  N61: R34.leg2, R35.leg2, R36.leg2, R37.leg2, R38.leg2, R39.leg2, R40.leg2, R41.leg2, R43.Pin_1
  N62: R35.wiper, S15.Pin_3, S15.Pin_4
  N63: R36.wiper, S14.Pin_3, S14.Pin_4
  N64: R37.wiper, S13.Pin_3, S13.Pin_4
  N65: R38.wiper, S12.Pin_3, S12.Pin_4
  N66: R39.wiper, S11.Pin_3, S11.Pin_4
  N67: R40.wiper, S10.Pin_3, S10.Pin_4
  N68: R41.wiper, S9.Pin_3, S9.Pin_4
  N69: R42.Pin_0, R53.Pin_1, C9.+
  N70: R50.Pin_0, C10.-
  N71: R61.Pin_0, R62.Pin_1, C10.+
  N72: C9.-, Audio_Out1.pin1
  N73: LDR3.pin_1, R63.Pin_0
  N74: R64.Pin_1, Adjust_to_60k1.leg2

notes:
  PWM Adjustment
